# Fritzing sketch chickencoop (saved by Fritzing 0.9.3b)

parts:
  Raspberry_Pi_Zero1 = Raspberry Pi Zero
  M3 = DC Motor
  S1 = H-Bridge with L298N
  S3 = Pushbutton [package=THT]
  S4 = Pushbutton [package=THT]
  BAT1 = Battery Holders [package=battcon_245mm_pth]

nets:
  N1: Raspberry_Pi_Zero1.GPIO17, S3.leg0
  N2: Raspberry_Pi_Zero1.GPIO22, S4.leg0
  N3: M3.pin_1, S1.M2-02
  N4: M3.pin_2, S1.M2-01
  N5: S1.12V, BAT1.-
  N6: S1.GND, BAT1.+
  N7: S1.IN3, S4.leg1
  N8: S1.IN4, S3.leg1

custom parts:
  H-Bridge with L298N: h-bridge
